# Fritzing sketch RespiradorDQ3D3 con shield (saved by Fritzing 0.9.4)
circuit board: 8.46667cm x 5.64444cm

parts:
  Componente1 = Arduino Nano (Rev3.0)
  M1 = Stepper Motor - Bipolar
  U1 = prefix0000
  Sensor_posicion_motor = CNZ1120 [package=cnz1120]
  R3 = Resistor [tolerance=±5% resistance=470 part_number="Cambiado de 10 k, cable largo" package=THT]
  R6 = Rotary Potentiometer (Large) [maximum_resistance=10kΩ package=THT]
  R7 = Rotary Potentiometer (Large) [maximum_resistance=10kΩ package=THT]
  Sensor_posicion_brazo = CNZ1120 [package=cnz1120]
  R9 = Resistor [tolerance=±5% resistance=470 part_number="Cambiado de 10 k, cable largo" package=THT]
  BMP280_presion_temp = Barometric Pressure Sensor - BMP180 Breakout (GY-68)
  Boton_reset = Pushbutton [package="[SMD]"]
  R1 = Resistor [tolerance=±5% resistance=5k package=THT]
  LED1 = LED - 5mm [color="White (4500K)" package="5 mm [THT]"]
  Power_good_de_Fuente = Resistor [tolerance=±5% resistance=5k package=THT]
  BMP280_presion_temp1 = Barometric Pressure Sensor - BMP180 Breakout (GY-68)
  12V_de_Fuente = Power plug
  Switch2 = Taiway 100-SP-X-T1 SPDT Miniature Toggle Switch [part_number="Inicio Ciclo" package=THT]
  R10 = Resistor [tolerance=±5% resistance=220 package=THT]
  J1 = Piezo Speaker [part_number="Alarma piezzo"]
  PS-ON_de_fuente = Taiway 100-SP-X-T1 SPDT Miniature Toggle Switch [part_number="Encendido principal" package=THT]
  LED2 = LED - 5mm [color="Red (635nm)" package="5 mm [THT]"]
  R11 = Resistor [tolerance=±5% resistance=5k package=THT]
  Switch_puerta_abierta = Limit Switch [package="Breakout Board"]
  J2 = female pin header, 2 pins [form="♀ (female)"]
  Mod1 = Nano-V3-0-IO-Expansion-Adapter
  U2 = 74HC595 [package="DIP16 [THT]"]
  R12 = Resistor [tolerance=±5% resistance=200 package=THT]
  LED4 = smd LED [color="Red (633nm)" package="1206 [SMD]"]
  R13 = Resistor [tolerance=±5% resistance=200 package=THT]
  LED5 = smd LED [color="Red (633nm)" package="1206 [SMD]"]
  R14 = Resistor [tolerance=±5% resistance=200 package=THT]
  LED6 = smd LED [color="Red (633nm)" package="1206 [SMD]"]
  R15 = Resistor [tolerance=±5% resistance=200 package=THT]
  LED7 = smd LED [color="Red (633nm)" package="1206 [SMD]"]
  R16 = Resistor [tolerance=±5% resistance=200 package=THT]
  LED8 = smd LED [color="Red (633nm)" package="1206 [SMD]"]
  R17 = Resistor [tolerance=±5% resistance=200 package=THT]
  LED9 = smd LED [color="Red (633nm)" package="1206 [SMD]"]
  R18 = Resistor [tolerance=±5% resistance=200 package=THT]
  LED10 = smd LED [color="Red (633nm)" package="1206 [SMD]"]
  R19 = Resistor [tolerance=±5% resistance=200 package=THT]
  LED3 = smd LED [color="Red (633nm)" package="1206 [SMD]"]

nets:
  N1: Componente1.D1/TX, Mod1.D1/TX#65, Mod1.D0/RX#128
  N2: Componente1.D0/RX, Mod1.D0/RX#64, Mod1.D1/TX#129
  N3: Componente1.RESET, Mod1.RST
  GND: Componente1.GND, U1.connector6, U1.connector8, U1.connector10, Sensor_posicion_motor.2, Sensor_posicion_motor.3, R6.leg1, R7.leg1, Sensor_posicion_brazo.2, Sensor_posicion_brazo.3, BMP280_presion_temp.GND, Boton_reset.Pin_1, Boton_reset.Pin_2, R1.Pin_0, Power_good_de_Fuente.Pin_0, BMP280_presion_temp1.GND, J1.pin1, PS-ON_de_fuente.L2, LED2.anode, Mod1.GND, U2.OE, LED3.cathode
  N4: Componente1.D2, Boton_reset.Pin_3, Mod1.D2
  N5: Componente1.D3, Mod1.D3_PWM
  N6: Componente1.D4, Sensor_posicion_motor.4, R3.Pin_0, Mod1.D4
  N7: Componente1.D5, U1.connector9, Mod1.D5_PWM
  N8: Componente1.D6, U1.connector11, Mod1.D6_PWM
  N9: Componente1.D7, R1.Pin_1, Switch2.L2, Mod1.D7
  N10: Componente1.D8, U1.connector7, Mod1.D8
  N11: Componente1.D9, Sensor_posicion_brazo.4, R9.Pin_0, Mod1.D9_PWM
  N12: Componente1.D10, Mod1.D10_PWM/SS, U2.DS
  N13: Componente1.D11/MOSI, Mod1.D11_PWM/MOSI, U2.ST_CP
  N14: Componente1.D12/MISO, Mod1.D12/MISO, U2.SH_CP
  VIN: Componente1.VIN, Mod1.VIN
  VCC: Componente1.5V, Sensor_posicion_motor.1, R3.Pin_1, R6.leg2, R7.leg2, Sensor_posicion_brazo.1, R9.Pin_1, Switch2.COM, Switch_puerta_abierta.V, Mod1.VCC, U2.MR, U2.VCC
  N15: Componente1.A7, Mod1.A7
  N16: Componente1.A6, Mod1.A6
  N17: Componente1.A5, BMP280_presion_temp.SCL, BMP280_presion_temp1.SCL, Mod1.A5/SCL
  N18: Componente1.A4, BMP280_presion_temp.SDA, BMP280_presion_temp1.SDA, Mod1.A4/SDA
  N19: Componente1.A3, Mod1.A3
  N20: Componente1.A2, Mod1.A2
  N21: Componente1.A1, R6.wiper, Mod1.A1
  N22: Componente1.A0, R7.wiper, Mod1.A0
  N23: Componente1.AREF, Mod1.AREF
  N24: Componente1.3V3, Mod1.NC
  N25: Componente1.D13/SCK, R10.Pin_0, Mod1.D13/SCK
  N26: M1.A, U1.connector3
  N27: M1.C, U1.connector2
  N28: M1.B, U1.connector1
  N29: M1.D, U1.connector0
  N30: U1.connector4, 12V_de_Fuente.VCC
  N31: U1.connector5, 12V_de_Fuente.GND
  VCC_2: BMP280_presion_temp.VCC, BMP280_presion_temp1.VCC, Mod1.3V3
  N32: LED1.cathode, J2.pin1
  N33: LED1.anode, Power_good_de_Fuente.Pin_1
  N34: R10.Pin_1, J1.pin2
  N35: PS-ON_de_fuente.COM, PS-ON_de_fuente.L1, J2.pin2
  N36: LED2.cathode, R11.Pin_0
  N37: R11.Pin_1, Switch_puerta_abierta.G
  N38: U2.Q1, R16.Pin_0
  N39: U2.Q2, R17.Pin_0
  N40: U2.Q3, R18.Pin_0
  N41: U2.Q4, R15.Pin_0
  N42: U2.Q5, R19.Pin_0
  N43: U2.Q6, R13.Pin_0
  N44: U2.Q7, R12.Pin_0
  N45: U2.Q0, R14.Pin_0
  N46: R12.Pin_1, LED3.anode
  N47: LED4.anode, R13.Pin_1
  N48: LED5.anode, R14.Pin_1
  N49: LED6.anode, R15.Pin_1
  N50: LED7.anode, R16.Pin_1
  N51: LED8.anode, R17.Pin_1
  N52: LED9.anode, R18.Pin_1
  N53: LED10.anode, R19.Pin_1

notes:
  Equipo Apoyo Respiratorio DQ3D-NICA
  Managua, 1 Agosto 2020

custom parts:
  Limit Switch: Generic limit switch commonly found on 3D printers. Typical lever microswitch mounted on a PCB board with a 3 pin JST XH connector.
  Nano-V3-0-IO-Expansion-Adapter: Nano V3.0 IO Expansion Adapter Shield. Note pcb view has been supressed as not useful. You can drag a Nano over the Nano connectors and it will connect and appear in schematic (although at present due to a bug, routing will not show as complete in breadboard).
